# Fritzing sketch Transmitter (saved by Fritzing 0.9.3b)
circuit board: 10cm x 8cm
breadboards: 2

parts:
  C1 = Electrolytic Capacitor [capacitance=1µF package="100 mil [THT, electrolytic]"]
  MUX1 = 74HC4051 [part_number=Menu package="DIP (Dual Inline) [THT]"]
  MUX2 = 74HC4051 [part_number=Trim package="DIP (Dual Inline) [THT]"]
  MUX3 = 74HC4051 [part_number=Switch package="DIP (Dual Inline) [THT]"]
  J1 = female pin header, 2 pins [form="♀ (female)" part_number=nRF24L01-power]
  J2 = female pin header, 6 pins [form="♀ (female)" part_number=nRF24L01-Header]
  D1 = Diode [package=diode-1n4001]
  VCC1 = Battery block 9V [part_number=9V-bat]
  R4 = Resistor [tolerance=±1% resistance=2.7k part_number="Vin-pre 1.2" power=250mW package=THT]
  IC1 = Voltage Regulator [part_number=7805 package=to-220-alt]
  R5 = Resistor [tolerance=±0.1% resistance=0.47 part_number=Shunt-amp power=1W package=THT]
  J6 = female pin header, 4 pins [form="♀ (female)" part_number=3.3v-I2C]
  R7 = Resistor [tolerance=±5% resistance=10k power=250mW package=THT]
  V1 = DC Power [voltage=5 part_number=VCC-NA]  # not connected
  R8 = Resistor [tolerance=±5% resistance=10k part_number=i2c-sda power=250mW package=THT]
  R9 = Resistor [tolerance=±5% resistance=10k part_number=i2c-sdc power=250mW package=THT]
  U2 = 74HC4052 [package=dil16]
  J4 = female pin header, 4 pins [form="♀ (female)" part_number="Serail Port"]
  R10 = Resistor [tolerance=±1% resistance=3.3k part_number="5v div 3.2" power=250mW package=THT]
  R11 = Resistor [tolerance=±1% resistance=2.2k part_number="5v div 3.1" power=250mW package=THT]
  LED1 = LED - 5mm [color="Green (570nm)" part_number=led-pwr package="5 mm [THT]"]
  R14 = Resistor [tolerance=±5% resistance=1k power=250mW package=THT]
  R15 = Resistor [tolerance=±1% resistance=8.2k part_number="Vin-post 2.1" power=250mW package=THT]
  R16 = Resistor [tolerance=±1% resistance=2.7k part_number="Vin-post 2.2" power=250mW package=THT]
  LCM1602_IIC1 = LCM1602 IIC [part_number="LCM1602 IIC" chip_label="LCM1602 IIC" package="DIP (Dual Inline) [THT]"]
  R17 = Resistor [tolerance=±5% resistance=1k part_number=warn power=250mW package=THT]
  LED2 = LED - 5mm [color="Red (633nm)" part_number=led-err package="5 mm [THT]"]
  J7 = female pin header, 6 pins [form="♀ (female)" part_number="AUX-CTL 2103"]
  SG1 = Buzzer 12mm [part_number="12mm buzzer" package=buzzer-12mm]
  J8 = female pin header, 3 pins [form="♀ (female)" part_number="1 wireKey"]
  J9 = female pin header, 4 pins [form="♀ (female)" part_number=5.0v-I2C]
  J5 = female pin header, 6 pins [form="♀ (female)" part_number=Joystick-CTL]
  J10 = female pin header, 6 pins [form="♀ (female)" part_number=Switch-4675]
  J11 = female pin header, 6 pins [form="♀ (female)" part_number=Trim-4675]
  J13 = female pin header, 6 pins [form="♀ (female)" part_number=Btn-2103]
  J14 = female pin header, 6 pins [form="♀ (female)" part_number=Trim-2103]
  J15 = female pin header, 6 pins [form="♀ (female)" part_number=Switch-2103]
  Q1 = TRANSISTOR_NPN [part_number=2n2222 package=to-92]
  Q2 = TRANSISTOR_NPN [part_number=2n2222 package=to-92]
  R18 = Resistor [tolerance=±5% resistance=10k part_number=warn power=250mW package=THT]
  R19 = Resistor [tolerance=±5% resistance=10k power=250mW package=THT]
  C2 = Electrolytic Capacitor [capacitance=1µF package="100 mil [THT, electrolytic]"]
  Part4 = NRF24L01+ Breakout Board
  Part1 = Arduino Nano (Rev3.0) [part_number="Arduino Nano (3.0)"]
  R20 = Resistor [tolerance=±5% resistance=3.6k power=250mW package=THT]
  J16 = female pin header, 4 pins [form="♀ (female)" part_number=5.0v-I2C]
  J12 = female pin header, 6 pins [form="♀ (female)"]
  J17 = JST-VHR-3N [part_number=JST-VHR-3N package=THT]  # not connected
  R3 = Resistor [tolerance=±1% resistance=8.2k part_number="Vin-pre 1.1" power=250mW package=THT]
  T1 = LM35 Temperature Sensor [part_number=LM336Z-5.0V package="TO92 [THT]"]
  U3 = ACS712 [part_number=ACS712 package=so08]  # not connected

nets:
  GND: C1.-, MUX1.INH, MUX1.VEE, MUX1.VSS, MUX2.INH, MUX2.VEE, MUX2.VSS, MUX3.INH, MUX3.VEE, MUX3.VSS, J1.pin2, VCC1.-, R4.Pin_1, IC1.GND, J6.pin2, U2.INH, U2.VEE, U2.GND, J4.pin2, R10.Pin_1, R14.Pin_0, R16.Pin_1, LCM1602_IIC1.GND, J7.pin2, J8.pin2, J9.pin2, J5.pin2, J10.pin2, J11.pin2, J13.pin2, J14.pin2, J15.pin2, Q1.E, Q2.E, C2.-, Part4.GND, Part1.GND, J16.pin2, J12.pin2, T1.+Vs
  N1: C1.+, J6.pin1, Part1.3V3
  N2: MUX1.IO4, J12.pin6
  N3: MUX1.IO6, J12.pin5
  N4: MUX1.IO, Part1.D8
  N5: MUX1.IO7, J12.pin4
  N6: MUX1.IO5, J12.pin3
  N7: MUX1.C, MUX2.C, MUX3.C, Part1.D3
  N8: MUX1.B, MUX2.B, MUX3.B, U2.B, Part1.D4
  N9: MUX1.A, MUX2.A, MUX3.A, U2.A, Part1.D5
  N10: MUX1.IO3, J13.pin3
  N11: MUX1.IO0, J13.pin4
  N12: MUX1.IO1, J13.pin5
  N13: MUX1.IO2, J13.pin6
  VDD: MUX1.VDD, MUX2.VDD, MUX3.VDD, J1.pin1, IC1.OUT, R7.Pin_0, R8.Pin_0, R9.Pin_0, U2.VCC, J4.pin1, R11.Pin_0, LCM1602_IIC1.VCC, LED2.anode, J7.pin1, SG1.1, J8.pin1, J9.pin1, J5.pin1, J10.pin1, J11.pin1, J13.pin1, J14.pin1, J15.pin1, C2.+, J16.pin1, J12.pin1
  N14: MUX2.IO4, J11.pin6
  N15: MUX2.IO6, J11.pin5
  N16: MUX2.IO, Part1.D7
  N17: MUX2.IO7, J11.pin4
  N18: MUX2.IO5, J11.pin3
  N19: MUX2.IO3, J14.pin3
  N20: MUX2.IO0, J14.pin4
  N21: MUX2.IO1, J14.pin5
  N22: MUX2.IO2, J14.pin6
  N23: MUX3.IO4, J10.pin6
  N24: MUX3.IO6, J10.pin5
  N25: MUX3.IO, Part1.D6
  N26: MUX3.IO7, J10.pin4
  N27: MUX3.IO5, J10.pin3
  N28: MUX3.IO3, J15.pin3
  N29: MUX3.IO0, J15.pin4
  N30: MUX3.IO1, J15.pin5
  N31: MUX3.IO2, J15.pin6
  N32: J2.pin1, Part4.CE, Part1.D9
  N33: J2.pin2, Part4.CS, Part1.D10
  N34: J2.pin3, Part4.SCK, Part1.D13/SCK
  N35: J2.pin4, Part4.MOSI, Part1.D11/MOSI
  N36: J2.pin5, Part4.MISO, Part1.D12/MISO
  N37: J2.pin6, Part4.IRQ
  N38: D1.A, VCC1.+
  N39: D1.C, R5.Pin_1, R3.Pin_0
  N40: R4.Pin_0, U2.Y3, R3.Pin_1
  N41: IC1.IN, R5.Pin_0, R15.Pin_0, R20.Pin_0
  N42: J6.pin3, R9.Pin_1, LCM1602_IIC1.SCL, J9.pin3, Part1.A5, J16.pin3
  N43: J6.pin4, R8.Pin_1, LCM1602_IIC1.SDA, J9.pin4, Part1.A4, J16.pin4
  N44: R7.Pin_1, Part1.RESET
  N45: U2.Y0, R15.Pin_1, R16.Pin_0
  N46: U2.Y2, R10.Pin_0, R11.Pin_1
  N47: U2.Y, Part1.A6
  N48: U2.Y1, J8.pin3
  N49: U2.X3, J7.pin3
  N50: U2.X0, J7.pin4
  N51: U2.X, Part1.A7
  N52: U2.X1, J7.pin5
  N53: U2.X2, J7.pin6
  N54: J4.pin3, Part1.D1/TX
  N55: J4.pin4, Part1.D0/RX
  N56: LED1.cathode, R14.Pin_1
  N57: LED1.anode, Part1.5V
  N58: R17.Pin_0, Q1.C
  N59: R17.Pin_1, LED2.cathode
  N60: SG1.2, Q2.C
  N61: J5.pin3, Part1.A3
  N62: J5.pin4, Part1.A2
  N63: J5.pin5, Part1.A1
  N64: J5.pin6, Part1.A0
  N65: Q1.B, R18.Pin_0
  N66: Q2.B, R19.Pin_0
  N67: R18.Pin_1, R19.Pin_1, Part1.D2
  N68: Part1.AREF, R20.Pin_1, T1.Vout, T1.GND

notes:
  2.4G Transmitter
  Q-Bytes World
  V1.1.4
  -+
  IRQ
  MI
  MO
  SCK
  CSN
  CE
  6-12v
  Y0231

custom parts:
  74HC4051: 8 channel analog multiplexer/demultiplexer
  LCM1602 IIC: I2C-Module to use a 1602 or 2004 LCD on with the wire.h libory Serial LCD Modul
