# Fritzing sketch Transmitter menu (saved by Fritzing 0.9.3b)
circuit board: 4.3cm x 4.3cm
breadboards: 1

parts:
  S1 = Pushbutton [package="[THT]"]
  R5 = Resistor [tolerance=±5% resistance=10k package=THT]
  S2 = Pushbutton [package="[THT]"]
  S3 = Pushbutton [package="[THT]"]
  S4 = Pushbutton [package="[THT]"]
  S5 = Pushbutton [package="[THT]"]
  J1 = female pin header, 3 pins [form="♀ (female)"]
  R4 = Resistor [tolerance=±5% resistance=10k package=THT]
  R3 = Resistor [tolerance=±5% resistance=10k package=THT]
  R2 = Resistor [tolerance=±5% resistance=10k package=THT]
  R0 = Resistor [tolerance=±5% resistance=1M package=THT]
  R1 = Resistor [tolerance=±5% resistance=10k package=THT]

nets:
  5V: S1.Pin_1, S1.Pin_2, J1.pin1, R1.Pin_0
  N1: S1.Pin_3, S1.Pin_4, S2.Pin_3, S2.Pin_4, S3.Pin_3, S3.Pin_4, S4.Pin_3, S4.Pin_4, S5.Pin_3, S5.Pin_4, J1.pin3, R0.Pin_1
  N2: R5.Pin_0, S5.Pin_1, S5.Pin_2, R4.Pin_1
  GND: R5.Pin_1, J1.pin2, R0.Pin_0
  N3: S2.Pin_1, S2.Pin_2, R2.Pin_0, R1.Pin_1
  N4: S3.Pin_1, S3.Pin_2, R3.Pin_0, R2.Pin_1
  N5: S4.Pin_1, S4.Pin_2, R4.Pin_0, R3.Pin_1

notes:
  -+
  Menu Control
  Q-Bytes World
  V1.0.6
