# Fritzing sketch Transmitter trim (saved by Fritzing 0.9.3b)
circuit board: 4.3cm x 1.2cm
breadboards: 1

parts:
  J1 = female pin header, 4 pins [form="♀ (female)"]
  S1 = Pushbutton [package="[THT]"]
  R1 = Resistor [tolerance=±5% resistance=10k package=THT]
  S2 = Pushbutton [package="[THT]"]
  R2 = Resistor [tolerance=±5% resistance=10k package=THT]

nets:
  5V: J1.pin1, S1.Pin_1, S1.Pin_2, S2.Pin_1, S2.Pin_2
  GND: J1.pin2, R1.Pin_1, R2.Pin_1
  N1: J1.pin3, S1.Pin_3, S1.Pin_4, R1.Pin_0
  N2: J1.pin4, S2.Pin_3, S2.Pin_4, R2.Pin_0

notes:
  -+
  Trim Control
  Q-Bytes World
  V1.0.8
