# Fritzing sketch ConstantCurrent_DummyLoad (saved by Fritzing 0.9.3b)
circuit board: 10cm x 5.64444cm
breadboards: 3

parts:
  U1 = LM124-324 Quad Opamp [part_number=LM324 package="DIP (Dual Inline)"]
  F1 = Fan - Ventilador [package=THT]
  Part1 = LCD1602-I2C
  Part2 = Arduino Nano (Rev3.0) (ICSP) [part_number="Nano 3.0"]
  Q1 = MOSFET-NCHANNEL [part_number=BS170 package=to-92]
  Q4 = Basic FET P-Channel [part_number=50N06 package="TO220 [THT]"]
  D1 = Rectifier Diode [part_number=1N4001 package="300 mil [THT]"]
  D2 = Rectifier Diode [part_number=1N4001 package="300 mil [THT]"]
  D3 = Rectifier Diode [part_number=1N4001 package="300 mil [THT]"]
  D4 = Rectifier Diode [part_number=1N4001 package="300 mil [THT]"]
  D5 = Rectifier Diode [part_number=1N4001 package="300 mil [THT]"]
  BAT1 = BC9VPC [package=bc9vpc]
  C1 = Capacitor [part_number=100uF package=cap-pth-small2]
  C8 = Capacitor [part_number=100uF package=cap-pth-small2]
  R3 = Resistor [tolerance=±5% resistance=47k power=0.25W package=THT]
  THS = Temperature Sensor (Thermistor) [thermistor_type=NTC package=THT]
  R8 = Resistor [tolerance=±5% resistance=12k power=0.25W package=THT]
  R4 = Resistor [tolerance=±5% resistance=150k power=0.25W package=THT]
  Q2 = MOSFET-NCHANNEL [part_number=BS170 package=to-92]
  R9 = Resistor [tolerance=±5% resistance=1k power=0.25W package=THT]
  JP_I2C = Header 4 [package=molex-1x4_lock]
  JP_SRL = Header 4 [package=molex-1x4_lock]
  R11 = Resistor [tolerance=±1% resistance=1 power=3W package=THT]
  R12 = Resistor [tolerance=±1% resistance=1 power=3W package=THT]
  R13 = Resistor [tolerance=±1% resistance=1 power=3W package=THT]
  R14 = Resistor [tolerance=±1% resistance=1 power=3W package=THT]
  R15 = Resistor [tolerance=±1% resistance=1 power=3W package=THT]
  R16 = Resistor [tolerance=±1% resistance=1 power=3W package=THT]
  R17 = Resistor [tolerance=±1% resistance=1 power=3W package=THT]
  R18 = Resistor [tolerance=±1% resistance=1 power=3W package=THT]
  R19 = Resistor [tolerance=±1% resistance=1 power=3W package=THT]
  R20 = Resistor [tolerance=±1% resistance=1 power=3W package=THT]
  R11_2 = Resistor [tolerance=±5% resistance=470 power=0.25W package=THT]
  MOV1 = VA250LA40BP [part_number="50V MOV" package=VA250LA40BP]
  Q3 = Basic FET P-Channel [part_number=50N06 package="TO220 [THT]"]
  R7 = Resistor [tolerance=±5% resistance=1k power=0.25W package=THT]
  C5 = Capacitor [part_number=100uF package=cap-pth-small2]
  Pot2 = TRIMPOT [part_number=1K package=trimpot_pth_s3_lock]
  R5 = Resistor [tolerance=±5% resistance=1k power=0.25W package=THT]
  R24 = Resistor [tolerance=±5% resistance=1k power=0.25W package=THT]
  Fuse1 = Fuse with Handler [part_number="Htc-15m - 700mA Fuse"]
  PWR = Header 2 [package=molex-1x2_lock]
  C3 = Electrolytic Capacitor [capacitance=1μF package="100 mil [THT, electrolytic]"]
  LED_FAN = LED - 5mm [color="Red (633nm)" package="5 mm [THT]"]
  LED_OVR = LED - 5mm [color="Red (633nm)" package="5 mm [THT]"]
  LED_PWR = LED - 5mm [color="Red (633nm)" package="5 mm [THT]"]
  C7 = Tantalum Capacitor [capacitance=100nF package="100 mil [THT, tantalum]"]
  C6 = Tantalum Capacitor [capacitance=100nF package="100 mil [THT, tantalum]"]
  C12 = Electrolytic Capacitor [capacitance=100µF package="100 mil [THT, electrolytic]"]
  C4 = Electrolytic Capacitor [capacitance=100µF package="100 mil [THT, electrolytic]"]
  J2 = female pin header, 5 pins [form="♀ (female)"]  # not connected
  J3 = female pin header, 5 pins [form="♀ (female)"]  # not connected
  FAN = female pin header, 2 pins [form="♀ (female)"]
  OVER_C = female pin header, 2 pins [form="♀ (female)"]
  PWR_2 = female pin header, 2 pins [form="♀ (female)"]
  JP3_3 = female pin header, 2 pins [form="♀ (female)"]
  TH1 = female pin header, 2 pins [form="♀ (female)"]
  Pot1 = TRIMPOT [part_number=1K package=trimpot_pth_s3_lock]
  R2 = Resistor [tolerance=±5% resistance=82k power=0.25W package=THT]
  R8_2 = Resistor [tolerance=±5% resistance=470 power=0.25W package=THT]
  R1 = Resistor [tolerance=±5% resistance=470 power=0.25W package=THT]
  IC1 = Voltage Regulator [package=78xxl]
  R25 = Resistor [tolerance=±5% resistance=6.8k power=0.25W package=THT]
  R26 = Resistor [tolerance=±5% resistance=3.3k power=0.25W package=THT]
  R27 = Resistor [tolerance=±5% resistance=2.7k power=0.25W package=THT]
  R28 = Resistor [tolerance=±5% resistance=6.8k power=0.25W package=THT]
  J4 = female pin header, 3 pins [form="♀ (female)"]
  R30 = Resistor [tolerance=±5% resistance=12k power=0.25W part_number=12-15K package=THT]
  R31 = Rotary Potentiometer (Large) [maximum_resistance=100kΩ package=THT]
  0-50V_0-5A = BC9VPC [part_number="0-50V 0-5A" package=bc9vpc]
  PWR_TST = Header 2 [package=molex-1x2_lock]

nets:
  N1: U1.1OUT, R4.Pin_1, Q2.G, LED_FAN.anode, FAN.pin2
  N2: U1.1IN-, U1.2IN-, THS.pin_1, R8.Pin_0, TH1.pin1
  N3: U1.1IN+, R4.Pin_0, R27.Pin_1, R28.Pin_1
  VCC: U1.VCC+, Part1.VCC, Part2.VIN, D1.cathode, C1.1, R8.Pin_1, JP_I2C.1, JP_SRL.1, C3.+, LED_PWR.anode, C12.+, PWR_2.pin2, Pot1.CCW, IC1.OUT, R25.Pin_0, R28.Pin_0
  N4: U1.2IN+, R3.Pin_0, R25.Pin_1, R26.Pin_1
  N5: U1.2OUT, Q1.G, R3.Pin_1, LED_OVR.anode, OVER_C.pin2
  N6: U1.3OUT, Part2.A1, R11_2.Pin_1, R8_2.Pin_0
  N7: U1.3IN-, Part2.A0, Pot1.WIPER
  N8: U1.3IN+, Q2.S, J4.pin2, R31.wiper
  GND: U1.VCC-, F1.GND, Part1.GND, Part2.GND, Q1.D, D4.anode, D5.anode, C8.2, THS.pin_0, Q2.D, R9.Pin_0, JP_I2C.2, JP_SRL.2, R11.Pin_1, R12.Pin_1, R13.Pin_1, R14.Pin_1, R15.Pin_1, R16.Pin_1, R17.Pin_1, R18.Pin_1, R19.Pin_1, R20.Pin_1, MOV1.P$2, Pot2.CW, R5.Pin_0, R24.Pin_0, C3.-, C7.-, C6.-, C12.-, C4.-, TH1.pin2, IC1.GND, R26.Pin_0, R27.Pin_0, J4.pin1, R30.Pin_0, R31.leg1, 0-50V_0-5A.V-, PWR_TST.2
  N9: U1.4IN+, R7.Pin_0, C5.1
  N10: U1.4IN-, U1.4OUT, R2.Pin_1
  N11: F1.5V, Q1.S, D1.anode, C1.2
  N12: Part1.SDA, Part2.A4, JP_I2C.3
  N13: Part1.SCL, Part2.A5, JP_I2C.4
  N14: Part2.D1/TX, JP_SRL.3
  N15: Part2.D0/RX, JP_SRL.4
  N16: Part2.RESET, Part2.5V
  N17: Part2.A2, Pot2.WIPER
  N18: Part2.AREF, JP3_3.pin2
  N19: Part2.3V3, JP3_3.pin1
  N20: Q4.gate, R11_2.Pin_0, C7.+
  N21: Q4.drain, MOV1.P$1, Q3.drain, Fuse1.Connector2, R1.Pin_0, PWR_TST.1
  N22: Q4.source, R11.Pin_0, R12.Pin_0, R13.Pin_0, R14.Pin_0, R15.Pin_0, R16.Pin_0, R17.Pin_0, R18.Pin_0, R19.Pin_0, R20.Pin_0, Q3.source, R7.Pin_1, C5.2
  N23: D2.cathode, D3.cathode, C8.1, C4.+, IC1.IN
  N24: D2.anode, D4.cathode, BAT1.V-, PWR.1
  N25: D3.anode, D5.cathode, BAT1.V+, PWR.2
  N26: R9.Pin_1, LED_OVR.cathode, OVER_C.pin1
  N27: Q3.gate, C6.+, R8_2.Pin_1
  N28: Pot2.CCW, R1.Pin_1
  N29: R5.Pin_1, LED_FAN.cathode, FAN.pin1
  N30: R24.Pin_1, LED_PWR.cathode, PWR_2.pin1
  N31: Fuse1.Connector1, 0-50V_0-5A.V+
  N32: Pot1.CW, R2.Pin_0
  N33: J4.pin3, R30.Pin_1, R31.leg2

custom parts:
  Fan - Ventilador: Ventilador de 2 pines, se encuentra comunmente en computadoras de escritorio
  LCD1602-I2C: A standard character display, usually with 2x16 characters. Comes in many colors with LCM1602 IIC attached.
  VA250LA40BP: Varistor (V18za2p with hole size increased to .042 and breadboard vuiew fixed up.)
