# Fritzing sketch iPhoneChargerUSB (saved by Fritzing 0.9.3b)
circuit board: 3.4cm x 1.96359cm
breadboards: 1

parts:
  R2 = Resistor [tolerance=±5% resistance=27k package=THT]
  R3 = Resistor [tolerance=±5% resistance=22k package=THT]
  R4 = Resistor [tolerance=±5% resistance=33k package=THT]
  R1 = Resistor [tolerance=±5% resistance=22k package=THT]
  X2 = USB Connectors [part_number=USB-A package=usb-a-s]
  IC1 = Voltage Regulator [part_number=7805 package=78xxl]
  VCC1 = Battery block 9V [part_number="+ -"]

nets:
  GND: R2.Pin_0, R3.Pin_0, X2.GND, IC1.GND, VCC1.-
  N1: R2.Pin_1, R1.Pin_0, X2.D+
  N2: R3.Pin_1, R4.Pin_0, X2.D-
  N3: R4.Pin_1, R1.Pin_1, X2.VBUS, IC1.OUT
  N4: IC1.IN, VCC1.+

notes:
  2.7V
  D+
  2.0V
  D-
  5.0V

custom parts:
  USB Connectors: USB Connectors USB-B-PTH is fully proven SKU : PRT-00139 USB-miniB is fully proven SKU : PRT-00587 USB-A-PCB is untested. USB-A-H is throughly reviewed, but untested. Spark Fun Electronics SKU : PRT-00437 USB-B-SMT is throughly reviewed, but untested. Needs silkscreen touching up. USB-A-S has not been used/tested USB-MB-H has not been used/tested
